// Digital circuit SPI_Slave.dig as structural Verilog
module SPI_Slave (
  input  SCK,
  input  MOSI,
  input  SS,
  input  clk,
  input  in_5,
  input  in_6,
  input  Write,
  input  in_8,
  input  in_9,
  input  in_10,
  input  in_11,
  input  in_12,
  input  in_13,
  input  in_14,
  input  in_15,
  input  Read,
  output MISO
);

  wire and_3_out, and_4_out, and_5_out, and_6_out, and_7_out, and_8_out, and_11_out, multiplexer_1_out,
       multiplexer_2_out, multiplexer_3_out, multiplexer_4_out, multiplexer_5_out, multiplexer_6_out,
       multiplexer_7_out, multiplexer_8_out, multiplexer_9_out, multiplexer_10_out, multiplexer_11_out,
       multiplexer_12_out, multiplexer_13_out, multiplexer_14_out, multiplexer_15_out, multiplexer_16_out,
       multiplexer_17_out, multiplexer_18_out, multiplexer_19_out, multiplexer_20_out, multiplexer_21_out,
       multiplexer_22_out, multiplexer_23_out, multiplexer_24_out, multiplexer_25_out, multiplexer_26_out,
       multiplexer_27_out, multiplexer_28_out, multiplexer_29_out, multiplexer_30_out, multiplexer_31_out,
       multiplexer_32_out, multiplexer_33_out, multiplexer_34_out, multiplexer_35_out, multiplexer_36_out,
       nor_1_out, not_1_out, not_2_out, not_3_out, not_4_out, not_5_out, not_6_out, not_7_out, not_8_out,
       not_9_out, not_10_out, not_11_out, not_12_out, not_13_out, not_14_out, not_15_out, not_16_out,
       not_17_out, not_18_out, not_19_out, not_20_out, or_1_out, or_2_out, or_5_out, or_6_out, or_7_out,
       or_8_out, register_1_q, register_2_q, register_3_q, register_4_q, register_5_q, register_6_q,
       register_7_q, register_8_q, register_9_q, register_10_q, register_11_q, register_12_q, register_13_q,
       register_14_q, register_15_q, register_16_q, register_17_q, register_18_q, register_19_q,
       register_20_q, register_21_q, register_22_q, register_23_q, register_24_q, register_25_q,
       register_26_q, register_27_q, register_28_q, register_29_q, register_30_q, register_31_q,
       register_32_q, register_33_q, register_34_q, register_35_q, register_36_q, register_37_q,
       register_38_q, register_39_q, register_40_q, register_41_q, register_42_q, register_43_q,
       register_44_q, register_45_q, register_46_q, register_47_q, register_48_q, register_50_q,
       register_51_q, register_52_q, register_53_q, register_54_q, register_55_q, register_56_q,
       register_57_q, register_58_q, register_59_q, register_60_q, register_61_q, register_62_q,
       register_63_q, register_64_q, register_65_q, register_66_q, register_67_q, register_68_q,
       register_69_q, register_70_q, register_71_q, register_72_q, register_73_q, register_74_q,
       register_75_q, register_76_q, register_77_q, register_78_q, register_79_q, register_80_q,
       register_81_q, register_82_q, register_83_q, register_84_q, register_85_q, register_86_q,
       register_87_q, register_88_q, register_89_q, register_90_q, register_91_q, register_92_q,
       register_93_q, register_94_q, register_95_q, register_96_q, register_97_q, register_98_q,
       register_99_q, register_100_q, register_101_q;
  wire [1:0] and_2_out, and_9_out, or_4_out, or_9_out;

  not not_1 (not_1_out, clk);
  not not_2 (not_2_out, clk);
  Register register_1 (.D(and_3_out), .C(not_1_out), .en(1'b1), .Q(register_1_q));
  Register register_2 (.D(Write), .C(not_2_out), .en(1'b1), .Q(register_2_q));
  not not_3 (not_3_out, register_3_q);
  Register register_3 (.D(register_1_q), .C(not_1_out), .en(1'b1), .Q(register_3_q));
  not not_4 (not_4_out, register_4_q);
  Register register_4 (.D(register_2_q), .C(not_2_out), .en(1'b1), .Q(register_4_q));
  Register register_5 (.D(in_8), .C(Write), .en(1'b1), .Q(register_5_q));
  Register register_6 (.D(in_9), .C(Write), .en(1'b1), .Q(register_6_q));
  Register register_7 (.D(in_10), .C(Write), .en(1'b1), .Q(register_7_q));
  Register register_8 (.D(in_11), .C(Write), .en(1'b1), .Q(register_8_q));
  Register register_9 (.D(in_12), .C(Write), .en(1'b1), .Q(register_9_q));
  Register register_10 (.D(in_13), .C(Write), .en(1'b1), .Q(register_10_q));
  Register register_11 (.D(in_14), .C(Write), .en(1'b1), .Q(register_11_q));
  Register register_12 (.D(in_15), .C(Write), .en(1'b1), .Q(register_12_q));
  and and_1 (and_2_out[1], register_1_q, not_3_out);
  and and_2 (and_2_out[0], register_2_q, not_4_out);
  Multiplexer multiplexer_1 (.sel(in_6), .in_0(register_21_q), .in_1(1'b1), .out(multiplexer_1_out));
  Register register_13 (.D(register_5_q), .C(Write), .en(1'b1), .Q(register_13_q));
  Register register_14 (.D(register_6_q), .C(Write), .en(1'b1), .Q(register_14_q));
  Register register_15 (.D(register_7_q), .C(Write), .en(1'b1), .Q(register_15_q));
  Register register_16 (.D(register_8_q), .C(Write), .en(1'b1), .Q(register_16_q));
  Register register_17 (.D(register_9_q), .C(Write), .en(1'b1), .Q(register_17_q));
  Register register_18 (.D(register_10_q), .C(Write), .en(1'b1), .Q(register_18_q));
  Register register_19 (.D(register_11_q), .C(Write), .en(1'b1), .Q(register_19_q));
  Register register_20 (.D(register_12_q), .C(Write), .en(1'b1), .Q(register_20_q));
  Multiplexer #(.Selector_Bits(2)) multiplexer_2 (
    .sel(and_2_out), .in_0(multiplexer_1_out), .in_1(1'b0), .in_2(or_1_out), .in_3(register_21_q),
    .out(multiplexer_2_out));
  Multiplexer #(.Selector_Bits(2)) multiplexer_3 (
    .sel(and_2_out), .in_0(register_22_q), .in_1(register_21_q), .in_2(register_23_q), .in_3(register_22_q),
    .out(multiplexer_3_out));
  Multiplexer #(.Selector_Bits(2)) multiplexer_4 (
    .sel(and_2_out), .in_0(register_23_q), .in_1(register_22_q), .in_2(register_24_q), .in_3(register_23_q),
    .out(multiplexer_4_out));
  Multiplexer #(.Selector_Bits(2)) multiplexer_5 (
    .sel(and_2_out), .in_0(register_24_q), .in_1(register_23_q), .in_2(register_25_q), .in_3(register_24_q),
    .out(multiplexer_5_out));
  Multiplexer #(.Selector_Bits(2)) multiplexer_6 (
    .sel(and_2_out), .in_0(register_25_q), .in_1(or_2_out), .in_2(1'b0), .in_3(register_25_q),
    .out(multiplexer_6_out));
  Register register_21 (.D(multiplexer_2_out), .C(clk), .en(1'b1), .Q(register_21_q));
  Register register_22 (.D(multiplexer_3_out), .C(clk), .en(1'b1), .Q(register_22_q));
  Register register_23 (.D(multiplexer_4_out), .C(clk), .en(1'b1), .Q(register_23_q));
  Register register_24 (.D(multiplexer_5_out), .C(clk), .en(1'b1), .Q(register_24_q));
  Register register_25 (.D(multiplexer_6_out), .C(clk), .en(1'b1), .Q(register_25_q));
  or or_1 (or_1_out, register_21_q, register_22_q);
  or or_2 (or_2_out, register_24_q, register_25_q);
  Register register_26 (.D(register_13_q), .C(Write), .en(1'b1), .Q(register_26_q));
  Register register_27 (.D(register_14_q), .C(Write), .en(1'b1), .Q(register_27_q));
  Register register_28 (.D(register_15_q), .C(Write), .en(1'b1), .Q(register_28_q));
  Register register_29 (.D(register_16_q), .C(Write), .en(1'b1), .Q(register_29_q));
  Register register_30 (.D(register_17_q), .C(Write), .en(1'b1), .Q(register_30_q));
  Register register_31 (.D(register_18_q), .C(Write), .en(1'b1), .Q(register_31_q));
  Register register_32 (.D(register_19_q), .C(Write), .en(1'b1), .Q(register_32_q));
  Register register_33 (.D(register_20_q), .C(Write), .en(1'b1), .Q(register_33_q));
  or or_3 (or_4_out[0], register_22_q, register_24_q);
  or or_4 (or_4_out[1], register_23_q, register_24_q);
  Register register_34 (.D(register_26_q), .C(Write), .en(1'b1), .Q(register_34_q));
  Register register_35 (.D(register_27_q), .C(Write), .en(1'b1), .Q(register_35_q));
  Register register_36 (.D(register_28_q), .C(Write), .en(1'b1), .Q(register_36_q));
  Register register_37 (.D(register_29_q), .C(Write), .en(1'b1), .Q(register_37_q));
  Register register_38 (.D(register_30_q), .C(Write), .en(1'b1), .Q(register_38_q));
  Register register_39 (.D(register_31_q), .C(Write), .en(1'b1), .Q(register_39_q));
  Register register_40 (.D(register_32_q), .C(Write), .en(1'b1), .Q(register_40_q));
  Register register_41 (.D(register_33_q), .C(Write), .en(1'b1), .Q(register_41_q));
  Multiplexer #(.Selector_Bits(2)) multiplexer_7 (
    .sel(or_4_out), .in_0(register_5_q), .in_1(register_13_q), .in_2(register_26_q), .in_3(register_34_q),
    .out(multiplexer_7_out));
  Multiplexer #(.Selector_Bits(2)) multiplexer_8 (
    .sel(or_4_out), .in_0(register_6_q), .in_1(register_14_q), .in_2(register_27_q), .in_3(register_35_q),
    .out(multiplexer_8_out));
  Multiplexer #(.Selector_Bits(2)) multiplexer_9 (
    .sel(or_4_out), .in_0(register_7_q), .in_1(register_15_q), .in_2(register_28_q), .in_3(register_36_q),
    .out(multiplexer_9_out));
  Multiplexer #(.Selector_Bits(2)) multiplexer_10 (
    .sel(or_4_out), .in_0(register_8_q), .in_1(register_16_q), .in_2(register_29_q), .in_3(register_37_q),
    .out(multiplexer_10_out));
  Multiplexer #(.Selector_Bits(2)) multiplexer_11 (
    .sel(or_4_out), .in_0(register_9_q), .in_1(register_17_q), .in_2(register_30_q), .in_3(register_38_q),
    .out(multiplexer_11_out));
  Multiplexer #(.Selector_Bits(2)) multiplexer_12 (
    .sel(or_4_out), .in_0(register_10_q), .in_1(register_18_q), .in_2(register_31_q), .in_3(register_39_q),
    .out(multiplexer_12_out));
  Multiplexer #(.Selector_Bits(2)) multiplexer_13 (
    .sel(or_4_out), .in_0(register_11_q), .in_1(register_19_q), .in_2(register_32_q), .in_3(register_40_q),
    .out(multiplexer_13_out));
  Multiplexer #(.Selector_Bits(2)) multiplexer_14 (
    .sel(or_4_out), .in_0(register_12_q), .in_1(register_20_q), .in_2(register_33_q), .in_3(register_41_q),
    .out(multiplexer_14_out));
  Multiplexer multiplexer_15 (
    .sel(and_3_out), .in_0(register_42_q), .in_1(multiplexer_8_out), .out(multiplexer_15_out));
  Multiplexer multiplexer_16 (
    .sel(and_3_out), .in_0(register_43_q), .in_1(multiplexer_9_out), .out(multiplexer_16_out));
  Multiplexer multiplexer_17 (
    .sel(and_3_out), .in_0(register_44_q), .in_1(multiplexer_10_out), .out(multiplexer_17_out));
  Multiplexer multiplexer_18 (
    .sel(and_3_out), .in_0(register_45_q), .in_1(multiplexer_11_out), .out(multiplexer_18_out));
  Multiplexer multiplexer_19 (
    .sel(and_3_out), .in_0(register_46_q), .in_1(multiplexer_12_out), .out(multiplexer_19_out));
  Multiplexer multiplexer_20 (
    .sel(and_3_out), .in_0(register_47_q), .in_1(multiplexer_13_out), .out(multiplexer_20_out));
  Multiplexer multiplexer_21 (
    .sel(and_3_out), .in_0(register_48_q), .in_1(multiplexer_14_out), .out(multiplexer_21_out));
  Register register_42 (.D(multiplexer_7_out), .C(multiplexer_22_out), .en(1'b1), .Q(register_42_q));
  Register register_43 (.D(multiplexer_15_out), .C(multiplexer_22_out), .en(1'b1), .Q(register_43_q));
  Register register_44 (.D(multiplexer_16_out), .C(multiplexer_22_out), .en(1'b1), .Q(register_44_q));
  Register register_45 (.D(multiplexer_17_out), .C(multiplexer_22_out), .en(1'b1), .Q(register_45_q));
  Register register_46 (.D(multiplexer_18_out), .C(multiplexer_22_out), .en(1'b1), .Q(register_46_q));
  Register register_47 (.D(multiplexer_19_out), .C(multiplexer_22_out), .en(1'b1), .Q(register_47_q));
  Register register_48 (.D(multiplexer_20_out), .C(multiplexer_22_out), .en(1'b1), .Q(register_48_q));
  Register register_49 (.D(multiplexer_21_out), .C(multiplexer_22_out), .en(1'b1), .Q(MISO));
  not not_5 (not_5_out, clk);
  not not_6 (not_6_out, clk);
  Register register_50 (.D(Read), .C(not_5_out), .en(1'b1), .Q(register_50_q));
  Register register_51 (.D(nor_1_out), .C(not_6_out), .en(1'b1), .Q(register_51_q));
  not not_7 (not_7_out, register_55_q);
  not not_8 (not_8_out, SS);
  not not_9 (not_9_out, register_56_q);
  not not_10 (not_10_out, SS);
  not not_11 (not_11_out, register_54_q);
  not not_12 (not_12_out, SS);
  not not_13 (not_13_out, register_55_q);
  not not_14 (not_14_out, SS);
  not not_15 (not_15_out, register_56_q);
  not not_16 (not_16_out, SS);
  not not_17 (not_17_out, register_56_q);
  not not_18 (not_18_out, SS);
  Multiplexer multiplexer_22 (.sel(SS), .in_0(SCK), .in_1(clk), .out(multiplexer_22_out));
  and and_3 (and_3_out, register_56_q, register_55_q, register_54_q);
  and and_4 (and_4_out, register_54_q, not_7_out, not_8_out);
  and and_5 (and_5_out, register_54_q, not_9_out, not_10_out);
  and and_6 (and_6_out, not_11_out, register_55_q, register_56_q, not_12_out);
  and and_7 (and_7_out, not_13_out, register_56_q, not_14_out);
  and and_8 (and_8_out, register_55_q, not_15_out, not_16_out);
  not not_19 (not_19_out, register_52_q);
  Register register_52 (.D(register_50_q), .C(not_5_out), .en(1'b1), .Q(register_52_q));
  Register register_53 (.D(register_51_q), .C(not_6_out), .en(1'b1), .Q(register_53_q));
  and and_9 (and_9_out[1], register_50_q, not_19_out);
  and and_10 (and_9_out[0], register_51_q, not_20_out);
  not not_20 (not_20_out, register_53_q);
  or or_5 (or_5_out, and_4_out, and_5_out, and_6_out);
  or or_6 (or_6_out, and_7_out, and_8_out);
  and and_11 (and_11_out, not_17_out, not_18_out);
  Register register_54 (.D(or_5_out), .C(multiplexer_22_out), .en(1'b1), .Q(register_54_q));
  Register register_55 (.D(or_6_out), .C(multiplexer_22_out), .en(1'b1), .Q(register_55_q));
  Register register_56 (.D(and_11_out), .C(multiplexer_22_out), .en(1'b1), .Q(register_56_q));
  Multiplexer multiplexer_23 (.sel(in_5), .in_0(register_57_q), .in_1(1'b1), .out(multiplexer_23_out));
  nor nor_1 (nor_1_out, register_54_q, register_55_q, register_56_q);
  Multiplexer #(.Selector_Bits(2)) multiplexer_24 (
    .sel(and_9_out), .in_0(multiplexer_23_out), .in_1(1'b0), .in_2(or_7_out), .in_3(register_57_q),
    .out(multiplexer_24_out));
  Multiplexer #(.Selector_Bits(2)) multiplexer_25 (
    .sel(and_9_out), .in_0(register_58_q), .in_1(register_57_q), .in_2(register_59_q), .in_3(register_58_q),
    .out(multiplexer_25_out));
  Multiplexer #(.Selector_Bits(2)) multiplexer_26 (
    .sel(and_9_out), .in_0(register_59_q), .in_1(register_58_q), .in_2(register_60_q), .in_3(register_59_q),
    .out(multiplexer_26_out));
  Multiplexer #(.Selector_Bits(2)) multiplexer_27 (
    .sel(and_9_out), .in_0(register_60_q), .in_1(register_59_q), .in_2(register_61_q), .in_3(register_60_q),
    .out(multiplexer_27_out));
  Multiplexer #(.Selector_Bits(2)) multiplexer_28 (
    .sel(and_9_out), .in_0(register_61_q), .in_1(or_8_out), .in_2(1'b0), .in_3(register_61_q),
    .out(multiplexer_28_out));
  Register register_57 (.D(multiplexer_24_out), .C(clk), .en(1'b1), .Q(register_57_q));
  Register register_58 (.D(multiplexer_25_out), .C(clk), .en(1'b1), .Q(register_58_q));
  Register register_59 (.D(multiplexer_26_out), .C(clk), .en(1'b1), .Q(register_59_q));
  Register register_60 (.D(multiplexer_27_out), .C(clk), .en(1'b1), .Q(register_60_q));
  Register register_61 (.D(multiplexer_28_out), .C(clk), .en(1'b1), .Q(register_61_q));
  Register register_62 (.D(MOSI), .C(SCK), .en(1'b1), .Q(register_62_q));
  Register register_63 (.D(register_62_q), .C(SCK), .en(1'b1), .Q(register_63_q));
  Register register_64 (.D(register_63_q), .C(SCK), .en(1'b1), .Q(register_64_q));
  Register register_65 (.D(register_64_q), .C(SCK), .en(1'b1), .Q(register_65_q));
  Register register_66 (.D(register_65_q), .C(SCK), .en(1'b1), .Q(register_66_q));
  Register register_67 (.D(register_66_q), .C(SCK), .en(1'b1), .Q(register_67_q));
  Register register_68 (.D(register_67_q), .C(SCK), .en(1'b1), .Q(register_68_q));
  Register register_69 (.D(register_68_q), .C(SCK), .en(1'b1), .Q(register_69_q));
  or or_7 (or_7_out, register_57_q, register_58_q);
  or or_8 (or_8_out, register_60_q, register_61_q);
  or or_9 (or_9_out[0], register_58_q, register_60_q);
  or or_10 (or_9_out[1], register_59_q, register_60_q);
  Register register_70 (.D(register_62_q), .C(and_9_out[0]), .en(1'b1), .Q(register_70_q));
  Register register_71 (.D(register_63_q), .C(and_9_out[0]), .en(1'b1), .Q(register_71_q));
  Register register_72 (.D(register_64_q), .C(and_9_out[0]), .en(1'b1), .Q(register_72_q));
  Register register_73 (.D(register_65_q), .C(and_9_out[0]), .en(1'b1), .Q(register_73_q));
  Register register_74 (.D(register_66_q), .C(and_9_out[0]), .en(1'b1), .Q(register_74_q));
  Register register_75 (.D(register_67_q), .C(and_9_out[0]), .en(1'b1), .Q(register_75_q));
  Register register_76 (.D(register_68_q), .C(and_9_out[0]), .en(1'b1), .Q(register_76_q));
  Register register_77 (.D(register_69_q), .C(and_9_out[0]), .en(1'b1), .Q(register_77_q));
  Register register_78 (.D(register_70_q), .C(and_9_out[0]), .en(1'b1), .Q(register_78_q));
  Register register_79 (.D(register_71_q), .C(and_9_out[0]), .en(1'b1), .Q(register_79_q));
  Register register_80 (.D(register_72_q), .C(and_9_out[0]), .en(1'b1), .Q(register_80_q));
  Register register_81 (.D(register_73_q), .C(and_9_out[0]), .en(1'b1), .Q(register_81_q));
  Register register_82 (.D(register_74_q), .C(and_9_out[0]), .en(1'b1), .Q(register_82_q));
  Register register_83 (.D(register_75_q), .C(and_9_out[0]), .en(1'b1), .Q(register_83_q));
  Register register_84 (.D(register_76_q), .C(and_9_out[0]), .en(1'b1), .Q(register_84_q));
  Register register_85 (.D(register_77_q), .C(and_9_out[0]), .en(1'b1), .Q(register_85_q));
  Register register_86 (.D(register_78_q), .C(and_9_out[0]), .en(1'b1), .Q(register_86_q));
  Register register_87 (.D(register_79_q), .C(and_9_out[0]), .en(1'b1), .Q(register_87_q));
  Register register_88 (.D(register_80_q), .C(and_9_out[0]), .en(1'b1), .Q(register_88_q));
  Register register_89 (.D(register_81_q), .C(and_9_out[0]), .en(1'b1), .Q(register_89_q));
  Register register_90 (.D(register_82_q), .C(and_9_out[0]), .en(1'b1), .Q(register_90_q));
  Register register_91 (.D(register_83_q), .C(and_9_out[0]), .en(1'b1), .Q(register_91_q));
  Register register_92 (.D(register_84_q), .C(and_9_out[0]), .en(1'b1), .Q(register_92_q));
  Register register_93 (.D(register_85_q), .C(and_9_out[0]), .en(1'b1), .Q(register_93_q));
  Register register_94 (.D(register_86_q), .C(and_9_out[0]), .en(1'b1), .Q(register_94_q));
  Register register_95 (.D(register_87_q), .C(and_9_out[0]), .en(1'b1), .Q(register_95_q));
  Register register_96 (.D(register_88_q), .C(and_9_out[0]), .en(1'b1), .Q(register_96_q));
  Register register_97 (.D(register_89_q), .C(and_9_out[0]), .en(1'b1), .Q(register_97_q));
  Register register_98 (.D(register_90_q), .C(and_9_out[0]), .en(1'b1), .Q(register_98_q));
  Register register_99 (.D(register_91_q), .C(and_9_out[0]), .en(1'b1), .Q(register_99_q));
  Register register_100 (.D(register_92_q), .C(and_9_out[0]), .en(1'b1), .Q(register_100_q));
  Register register_101 (.D(register_93_q), .C(and_9_out[0]), .en(1'b1), .Q(register_101_q));
  Multiplexer #(.Selector_Bits(2)) multiplexer_29 (
    .sel(or_9_out), .in_0(register_70_q), .in_1(register_78_q), .in_2(register_86_q), .in_3(register_94_q),
    .out(multiplexer_29_out));
  Multiplexer #(.Selector_Bits(2)) multiplexer_30 (
    .sel(or_9_out), .in_0(register_71_q), .in_1(register_79_q), .in_2(register_87_q), .in_3(register_95_q),
    .out(multiplexer_30_out));
  Multiplexer #(.Selector_Bits(2)) multiplexer_31 (
    .sel(or_9_out), .in_0(register_72_q), .in_1(register_80_q), .in_2(register_88_q), .in_3(register_96_q),
    .out(multiplexer_31_out));
  Multiplexer #(.Selector_Bits(2)) multiplexer_32 (
    .sel(or_9_out), .in_0(register_73_q), .in_1(register_81_q), .in_2(register_89_q), .in_3(register_97_q),
    .out(multiplexer_32_out));
  Multiplexer #(.Selector_Bits(2)) multiplexer_33 (
    .sel(or_9_out), .in_0(register_74_q), .in_1(register_82_q), .in_2(register_90_q), .in_3(register_98_q),
    .out(multiplexer_33_out));
  Multiplexer #(.Selector_Bits(2)) multiplexer_34 (
    .sel(or_9_out), .in_0(register_75_q), .in_1(register_83_q), .in_2(register_91_q), .in_3(register_99_q),
    .out(multiplexer_34_out));
  Multiplexer #(.Selector_Bits(2)) multiplexer_35 (
    .sel(or_9_out), .in_0(register_76_q), .in_1(register_84_q), .in_2(register_92_q), .in_3(register_100_q),
    .out(multiplexer_35_out));
  Multiplexer #(.Selector_Bits(2)) multiplexer_36 (
    .sel(or_9_out), .in_0(register_77_q), .in_1(register_85_q), .in_2(register_93_q), .in_3(register_101_q),
    .out(multiplexer_36_out));

  // Notes on the sheet:
  //   clk: Hz: 5
endmodule
